# Fritzing sketch Schema (saved by Fritzing 0.8.7b)
breadboards: 1

parts:
  Composant1 = Arduino Mega 2560 (Rev3)
  Raspberry_Pi_B_rev1 = Raspberry Pi B rev2
  IC1 = L293D [package=THT]
  S1 = Pushbutton [package="[THT]"]
  OLED1 = 1.27" 128x96 16-bit OLED Breakout
  S2 = Pushbutton [package="[THT]"]
  M1 = Stepper Motor - Bipolar
  R1 = Resistor [tolerance=±5% resistance=220 package=THT]
  R2 = Resistor [tolerance=±5% resistance=220 package=THT]
  R3 = Resistor [tolerance=±5% resistance=220 package=THT]
  S3 = Square Pushbutton

nets:
  N1: Composant1.D21/SCL, Raspberry_Pi_B_rev1.GPIO_3
  N2: Composant1.D20/SDA, Raspberry_Pi_B_rev1.GPIO_2
  5V: Composant1.5V, Raspberry_Pi_B_rev1.5V, IC1.+Vmotor, IC1.Enable_2, OLED1.+, R1.Pin_1, R2.Pin_1, R3.Pin_1
  GND: Composant1.GND, Raspberry_Pi_B_rev1.GND, IC1.Enable_1, IC1.0V, S1.Pin_3, S1.Pin_4, OLED1.G, S2.Pin_3, S2.Pin_4, S3.leg1
  N3: Composant1.D22, S2.Pin_1, S2.Pin_2, R2.Pin_0
  N4: Composant1.D24, S1.Pin_1, S1.Pin_2, R1.Pin_0
  N5: Composant1.D26, R3.Pin_0, S3.leg0
  N6: Composant1.D30, IC1.In_3
  N7: Composant1.D32, IC1.In_4
  N8: Composant1.D34, IC1.In_1
  N9: Composant1.D36, IC1.In_2
  N10: Composant1.D46, OLED1.SC
  N11: Composant1.D48, OLED1.DC
  N12: Composant1.D49, OLED1.R
  N13: Composant1.D50, OLED1.SO
  N14: Composant1.D51, OLED1.SI
  N15: Composant1.D52, OLED1.CL
  N16: Composant1.D53, OLED1.OC
  N17: IC1.Out_1_(_Controlled_by_Enable_1_), M1.B
  N18: IC1.Out_2_(_Controlled_by_Enable_1_), M1.D
  N19: IC1.Out_3_(_Controlled_by_Enable_2_), M1.A
  N20: IC1.Out_4_(_Controlled_by_Enable_2_), M1.C
